// Logisim project ex4.circ as structural Verilog: 5 circuits, main circuit RotRight
module RotRight (
  input  [15:0] INPUT0,
  input  [3:0] AMOUNT,
  output [15:0] OUTPUT0
);

  wire [15:0] next1, next2, next3, rot1_1_out_2, rot2_1_out_2, rot4_1_out_2, rot8_1_out_2;

  rot1 rot1_1 (.in_1(INPUT0), .out_2(rot1_1_out_2));
  Multiplexer #(.width(16)) multiplexer_1 (.in0(INPUT0), .in1(rot1_1_out_2), .out(next1), .sel(AMOUNT[0]));
  rot2 rot2_1 (.in_1(next1), .out_2(rot2_1_out_2));
  Multiplexer #(.width(16)) multiplexer_2 (.in0(next1), .in1(rot2_1_out_2), .out(next2), .sel(AMOUNT[1]));
  Multiplexer #(.width(16)) multiplexer_3 (.in0(next2), .in1(rot4_1_out_2), .out(next3), .sel(AMOUNT[2]));
  rot4 rot4_1 (.in_1(next2), .out_2(rot4_1_out_2));
  rot8 rot8_1 (.in_1(next3), .out_2(rot8_1_out_2));
  Multiplexer #(.width(16)) multiplexer_4 (.in0(next3), .in1(rot8_1_out_2), .out(OUTPUT0), .sel(AMOUNT[3]));

  // Other names for the same wires on the sheet: zero = AMOUNT[0]; one = AMOUNT[1]; two = AMOUNT[2];
  //   three = AMOUNT[3]; final[15:0] = OUTPUT0; self[15:0] = INPUT0
endmodule

module rot1 (
  input  [15:0] in_1,
  output [15:0] out_2
);


  assign out_2 = {in_1[0], in_1[15:1]};
endmodule

module rot2 (
  input  [15:0] in_1,
  output [15:0] out_2
);


  assign out_2 = {in_1[1:0], in_1[15:2]};
endmodule

module rot4 (
  input  [15:0] in_1,
  output [15:0] out_2
);


  assign out_2 = {in_1[3:0], in_1[15:4]};
endmodule

module rot8 (
  input  [15:0] in_1,
  output [15:0] out_2
);


  assign out_2 = {in_1[7:0], in_1[15:8]};
endmodule
