// Logisim project control-logic.circ as structural Verilog: 1 circuit, main circuit control_logic
module control_logic (
  input  [31:0] Instruction,
  input  BrEq,
  input  BrLt,
  output PCSel,
  output RegWEn,
  output [2:0] ImmSel,
  output BrUn,
  output ASel,
  output BSel,
  output [3:0] ALUSel,
  output MemWEn,
  output [1:0] WBSel
);

  wire and_25_out, and_26_out, and_27_out, and_28_out, and_29_out, and_30_out, func3_0, func3_1, func3_2,
       func3_3, func3_4, func3_5, func3_6, func3_7, func7_0000000, func7_0000001, func7_0100000,
       instruction_0, instruction_1, instruction_2, instruction_3, instruction_4, instruction_5,
       instruction_6, instruction_7, instruction_8, instruction_9, instruction_10, instruction_11,
       instruction_12, instruction_13, instruction_14, instruction_15, instruction_16, instruction_17,
       instruction_18, instruction_19, instruction_20, instruction_21, instruction_22, instruction_23,
       instruction_24, instruction_25, instruction_26, instruction_27, instruction_28, instruction_29,
       instruction_30, instruction_31, instruction_32, instruction_33, instruction_34, instruction_35, isB,
       isI1, isI2, isR, isS, not_1_out, not_2_out, not_3_out, not_4_out, not_5_out;
  wire [5:0] input0;
  wire [15:14] rom_1_data;

  and and_1 (instruction_0, isR, func3_0, func7_0000000);
  and and_2 (instruction_4, isR, func3_1, func7_0000001);
  and and_3 (instruction_8, isR, func3_5, func7_0000000);
  and and_4 (instruction_12, isI1, func3_0);
  and and_5 (instruction_24, isS, func3_1);
  and and_6 (instruction_28, isB, func3_4);
  Comparator #(.width(7)) comparator_1 (.a(Instruction[6:0]), .b(7'b0110011), .eq(isR));  // open: gt, lt
  Comparator #(.width(7)) comparator_2 (.a(Instruction[6:0]), .b(7'b0000011), .eq(isI1));  // open: gt, lt
  Comparator #(.width(7)) comparator_3 (.a(Instruction[6:0]), .b(7'b0010011), .eq(isI2));  // open: gt, lt
  Comparator #(.width(7)) comparator_4 (.a(Instruction[6:0]), .b(7'b0100011), .eq(isS));  // open: gt, lt
  Comparator #(.width(7)) comparator_5 (.a(Instruction[6:0]), .b(7'b1100011), .eq(isB));  // open: gt, lt
  Comparator #(.width(7)) comparator_6 (.a(Instruction[6:0]), .b(7'b0010111), .eq(instruction_32));  // open: gt, lt
  Comparator #(.width(7)) comparator_7 (.a(Instruction[6:0]), .b(7'b0110111), .eq(instruction_33));  // open: gt, lt
  Comparator #(.width(7)) comparator_8 (.a(Instruction[6:0]), .b(7'b1101111), .eq(instruction_34));  // open: gt, lt
  Comparator #(.width(7)) comparator_9 (.a(Instruction[6:0]), .b(7'b1100111), .eq(instruction_35));  // open: gt, lt
  and and_7 (instruction_16, isI2, func3_1, func7_0000000);
  and and_8 (instruction_20, isI2, func3_5, func7_0100000);
  ROM #(.addrWidth(6), .dataWidth(16)) rom_1 (
    .addr(input0), .data({rom_1_data, WBSel, MemWEn, ALUSel, BSel, ASel, BrUn, ImmSel, RegWEn}));
  Comparator #(.width(3)) comparator_10 (.a(Instruction[14:12]), .b(3'b000), .eq(func3_0));  // open: gt, lt
  Comparator #(.width(3)) comparator_11 (.a(Instruction[14:12]), .b(3'b001), .eq(func3_1));  // open: gt, lt
  Comparator #(.width(3)) comparator_12 (.a(Instruction[14:12]), .b(3'b010), .eq(func3_2));  // open: gt, lt
  Comparator #(.width(3)) comparator_13 (.a(Instruction[14:12]), .b(3'b011), .eq(func3_3));  // open: gt, lt
  Comparator #(.width(3)) comparator_14 (.a(Instruction[14:12]), .b(3'b100), .eq(func3_4));  // open: gt, lt
  Comparator #(.width(3)) comparator_15 (.a(Instruction[14:12]), .b(3'b101), .eq(func3_5));  // open: gt, lt
  Comparator #(.width(3)) comparator_16 (.a(Instruction[14:12]), .b(3'b110), .eq(func3_6));  // open: gt, lt
  Comparator #(.width(3)) comparator_17 (.a(Instruction[14:12]), .b(3'b111), .eq(func3_7));  // open: gt, lt
  and and_9 (instruction_17, isI2, func3_2);
  and and_10 (instruction_21, isI2, func3_6);
  and and_11 (instruction_1, isR, func3_0, func7_0000001);
  and and_12 (instruction_5, isR, func3_3, func7_0000001);
  and and_13 (instruction_9, isR, func3_5, func7_0100000);
  and and_14 (instruction_13, isI1, func3_1);
  and and_15 (instruction_25, isS, func3_2);
  and and_16 (instruction_29, isB, func3_5);
  Comparator #(.width(7)) comparator_18 (.a(Instruction[31:25]), .b({7{1'b0}}), .eq(func7_0000000));  // open: gt, lt
  Comparator #(.width(7)) comparator_19 (.a(Instruction[31:25]), .b(7'b0000001), .eq(func7_0000001));  // open: gt, lt
  Comparator #(.width(7)) comparator_20 (.a(Instruction[31:25]), .b(7'b0100000), .eq(func7_0100000));  // open: gt, lt
  and and_17 (instruction_14, isI1, func3_2);
  and and_18 (instruction_18, isI2, func3_4);
  and and_19 (instruction_22, isI2, func3_7);
  and and_20 (instruction_26, isB, func3_0);
  and and_21 (instruction_30, isB, func3_6);
  and and_22 (instruction_2, isR, func3_0, func7_0100000);
  and and_23 (instruction_6, isR, func3_2, func7_0000000);
  and and_24 (instruction_10, isR, func3_6, func7_0000000);
  not not_1 (not_1_out, BrEq);
  not not_2 (not_2_out, BrEq);
  not not_3 (not_3_out, BrLt);
  not not_4 (not_4_out, BrEq);
  not not_5 (not_5_out, BrLt);
  and and_25 (and_25_out, instruction_26, BrEq);
  and and_26 (and_26_out, instruction_27, not_1_out);
  and and_27 (and_27_out, instruction_28, BrLt, not_2_out);
  and and_28 (and_28_out, instruction_29, not_3_out, BrEq);
  and and_29 (and_29_out, instruction_30, BrLt, not_4_out, BrUn);
  and and_30 (and_30_out, instruction_31, not_5_out, BrEq, BrUn);
  and and_31 (instruction_3, isR, func3_1, func7_0000000);
  and and_32 (instruction_7, isR, func3_4, func7_0000000);
  and and_33 (instruction_11, isR, func3_7, func7_0000000);
  and and_34 (instruction_15, isI2, func3_0);
  and and_35 (instruction_19, isI2, func3_5, func7_0000000);
  and and_36 (instruction_23, isS, func3_0);
  and and_37 (instruction_27, isB, func3_1);
  and and_38 (instruction_31, isB, func3_7);
  or or_1 (PCSel, and_25_out, and_26_out, and_27_out, and_28_out, and_29_out, and_30_out, instruction_34, instruction_35);
  Priority_Encoder #(.select_enc(6)) priority_encoder_1 (
    .in0(instruction_0), .in1(instruction_1), .in2(instruction_2), .in3(instruction_3), .in4(instruction_4),
    .in5(instruction_5), .in6(instruction_6), .in7(instruction_7), .in8(instruction_8), .in9(instruction_9),
    .in10(instruction_10), .in11(instruction_11), .in12(instruction_12), .in13(instruction_13),
    .in14(instruction_14), .in15(instruction_15), .in16(instruction_16), .in17(instruction_17),
    .in18(instruction_18), .in19(instruction_19), .in20(instruction_20), .in21(instruction_21),
    .in22(instruction_22), .in23(instruction_23), .in24(instruction_24), .in25(instruction_25),
    .in26(instruction_26), .in27(instruction_27), .in28(instruction_28), .in29(instruction_29),
    .in30(instruction_30), .in31(instruction_31), .in32(instruction_32), .in33(instruction_33),
    .in34(instruction_34), .in35(instruction_35), .out(input0));  // open: in36, in37, in38, in39, in40, in41, in42, in43, in44, in45, in46, in47, in48, in49, in50, in51, in52, in53, in54, in55, in56, in57, in58, in59, in60, in61, in62, in63, gs, en_out, en_in

  // Other names for the same wires on the sheet: opcode[6:0] = Instruction[6:0]; func3[2:0] = Instruction[14:12];
  //   func7[6:0] = Instruction[31:25]; isI3 = instruction_35; isJ = instruction_34; isU1 = instruction_32;
  //   isU2 = instruction_33

  // Notes on the sheet:
  //   INPUTS to your circuit
  //   Connect ROM Input here ->
  //   CONNECT
  //   WIRE
  //   TO
  //   USE
  //   ROM
  //   contents of rom_1 (hex, n*v repeats v):
  //   100f 140f 160f 108f 148f 158f 110f 120f 128f 168f 130f 138f 41 41 41 1041 10c1 1141 1241 12c1 16c1
  //   1341 13c1 1842 1842 1842 4*1064 1074 1074 1067 17c7 2069 2041 10 18 11 19 100 20 101 21 110 22 111
  //   23 1000 24 1001 25 1010 26 1011 27 1100 28 1101 29 1110 30 1111 31
  //   ROM FOR CONTROL LOGIC
  //   DON'T CHANGE THE LOCATIONS OF THE INPUTS AND OUTPUTS!
  //   This is only if you choose to do the ROM option
  //   OUTPUT from your circuit
  //   Reminder: If using ROM, use combinational logic for PCSel
endmodule
