// Logisim project cpu.circ as structural Verilog: 1 circuit, main circuit cpu
module cpu (
  input  clk,
  input  [31:0] Instruction,
  input  [31:0] MemReadData,
  output [31:0] MemAddress,
  output [31:0] ProgramCounter,
  output [31:0] ra,
  output [31:0] sp,
  output [31:0] t0,
  output [31:0] t1,
  output [31:0] t2,
  output [31:0] s0,
  output [31:0] s1,
  output [31:0] a0,
  output [3:0] MemWriteMask,
  output [31:0] MemWriteData
);

  wire ASel, BrEq, BrLt, BrUn, Bsel, MemWEn, PCSel, RegWEn;
  wire [1:0] WBSel;
  wire [2:0] control_logic_1_immsel;
  wire [3:0] ALUSel;
  wire [4:0] rd, rs1, rs2;
  wire [31:0] adder_1_out, immrst, loadrst, multiplexer_1_out, multiplexer_2_out, multiplexer_3_out,
       multiplexer_4_out, multiplexer_5_out, rd1, rd2, register_1_q, register_2_q, subtractor_1_out;

  Adder #(.width(32)) adder_1 (.a(ProgramCounter), .b(32'h4), .out(adder_1_out));  // open: cin, cout
  Register #(.width(32)) PC (.D(multiplexer_1_out), .clk(clk), .Q(ProgramCounter));  // open: en, clr
  Multiplexer #(.width(32)) multiplexer_1 (.in0(adder_1_out), .in1(MemAddress), .out(multiplexer_1_out), .sel(PCSel));
  Register #(.width(32)) register_1 (.D(adder_1_out), .clk(clk), .Q(register_1_q));  // open: en, clr
  Multiplexer #(.width(32)) multiplexer_2 (.in0(Instruction), .in1(32'h13), .out(multiplexer_2_out), .sel(PCSel));
  Register #(.width(32)) register_2 (
    .D(multiplexer_2_out), .clk(clk),
    .Q({register_2_q[31:25], rs2, rs1, register_2_q[14:12], rd, register_2_q[6:0]}));  // open: en, clr
  control_logic control_logic_1 (
    .Instruction({register_2_q[31:25], rs2, rs1, register_2_q[14:12], rd, register_2_q[6:0]}), .BrEq(BrEq),
    .BrLt(BrLt), .PCSel(PCSel), .RegWEn(RegWEn), .ImmSel(control_logic_1_immsel), .BrUn(BrUn), .ASel(ASel),
    .BSel(Bsel), .ALUSel(ALUSel), .MemWEn(MemWEn), .WBSel(WBSel));
  Multiplexer #(.select(2), .width(32)) multiplexer_3 (
    .in0(loadrst), .in1(MemAddress), .in2(register_1_q), .out(multiplexer_3_out), .sel(WBSel));  // open: in3
  imm_gen imm_gen_1 (
    .Instruction({register_2_q[31:25], rs2, rs1, register_2_q[14:12], rd, register_2_q[6:0]}),
    .ImmSel(control_logic_1_immsel), .Immediate(immrst));
  regfile regfile_1 (
    .ReadIndex1(rs1), .ReadIndex2(rs2), .WriteIndex(rd), .WriteData(multiplexer_3_out), .RegWEn(RegWEn),
    .clk(clk), .ra(ra), .sp(sp), .t0(t0), .t1(t1), .t2(t2), .s0(s0), .s1(s1), .a0(a0), .ReadData1(rd1),
    .ReadData2(rd2));
  Subtractor #(.width(32)) subtractor_1 (.a(register_1_q), .b(32'h4), .out(subtractor_1_out));  // open: bin, bout
  branch_comp branch_comp_1 (.BrData1(rd1), .BrData2(rd2), .BrUn(BrUn), .BrEq(BrEq), .BrLt(BrLt));
  Multiplexer #(.width(32)) multiplexer_4 (.in0(rd1), .in1(subtractor_1_out), .out(multiplexer_4_out), .sel(ASel));
  Multiplexer #(.width(32)) multiplexer_5 (.in0(rd2), .in1(immrst), .out(multiplexer_5_out), .sel(Bsel));
  alu alu_1 (.A(multiplexer_4_out), .B(multiplexer_5_out), .ALUSel(ALUSel), .ALUResult(MemAddress));
  partial_store partial_store_1 (
    .Instruction({register_2_q[31:25], rs2, rs1, register_2_q[14:12], rd, register_2_q[6:0]}),
    .MemAddress(MemAddress), .DataFromReg(rd2), .MemWEn(MemWEn), .MemWriteMask(MemWriteMask),
    .DataToMem(MemWriteData));
  partial_load partial_load_1 (
    .Instruction({register_2_q[31:25], rs2, rs1, register_2_q[14:12], rd, register_2_q[6:0]}),
    .MemAddress(MemAddress), .DataFromMem(MemReadData), .DataToReg(loadrst));

  // Other names for the same wires on the sheet: ALUrst[31:0] = MemAddress

  // Notes on the sheet:
  //   To IMEM
  //   IMEM (do **NOT** move this)
  //   From IMEM
  //   Inputs/Outputs for testing. Do **NOT** move these.
  //   To DMEM
  //   DMEM (do **NOT** move this)
  //   From DMEM
endmodule
