// Logisim project regfile.circ as structural Verilog: 1 circuit, main circuit regfile
module regfile (
  input  [4:0] ReadIndex1,
  input  [4:0] ReadIndex2,
  input  [4:0] WriteIndex,
  input  [31:0] WriteData,
  input  RegWEn,
  input  clk,
  output [31:0] ra,
  output [31:0] sp,
  output [31:0] t0,
  output [31:0] t1,
  output [31:0] t2,
  output [31:0] s0,
  output [31:0] s1,
  output [31:0] a0,
  output [31:0] ReadData1,
  output [31:0] ReadData2
);

  wire comparator_1_eq, comparator_2_eq, comparator_3_eq, comparator_4_eq, comparator_5_eq, comparator_6_eq,
       comparator_7_eq, comparator_8_eq, comparator_9_eq, comparator_10_eq, comparator_11_eq,
       comparator_12_eq, comparator_13_eq, comparator_14_eq, comparator_15_eq, comparator_16_eq,
       comparator_17_eq, comparator_18_eq, comparator_19_eq, comparator_20_eq, comparator_21_eq,
       comparator_22_eq, comparator_23_eq, comparator_24_eq, comparator_25_eq, comparator_26_eq,
       comparator_27_eq, comparator_28_eq, comparator_29_eq, comparator_30_eq, comparator_31_eq;
  wire [31:0] a1, a2, a3, a4, a5, a6, a7, gp, multiplexer_1_out, multiplexer_2_out, multiplexer_3_out,
       multiplexer_4_out, multiplexer_5_out, multiplexer_6_out, multiplexer_7_out, multiplexer_8_out,
       multiplexer_9_out, multiplexer_10_out, multiplexer_11_out, multiplexer_12_out, multiplexer_13_out,
       multiplexer_14_out, multiplexer_15_out, multiplexer_16_out, multiplexer_18_out, multiplexer_19_out,
       multiplexer_20_out, multiplexer_21_out, multiplexer_22_out, multiplexer_23_out, multiplexer_24_out,
       multiplexer_25_out, multiplexer_27_out, multiplexer_28_out, multiplexer_29_out, multiplexer_30_out,
       multiplexer_31_out, multiplexer_32_out, multiplexer_33_out, s2, s3, s4, s5, s6, s7, s8, s9, s10, s11,
       t3, t4, t5, t6, tp;

  Comparator #(.mode("unsigned"), .width(5)) comparator_1 (
    .a(WriteIndex), .b(5'b00001), .eq(comparator_1_eq));  // open: gt, lt
  Comparator #(.mode("unsigned"), .width(5)) comparator_2 (
    .a(WriteIndex), .b(5'b00101), .eq(comparator_2_eq));  // open: gt, lt
  Comparator #(.mode("unsigned"), .width(5)) comparator_3 (
    .a(WriteIndex), .b(5'b01001), .eq(comparator_3_eq));  // open: gt, lt
  Comparator #(.mode("unsigned"), .width(5)) comparator_4 (
    .a(WriteIndex), .b(5'b01101), .eq(comparator_4_eq));  // open: gt, lt
  Multiplexer #(.width(32)) multiplexer_1 (.in0(a7), .in1(WriteData), .out(multiplexer_1_out), .sel(comparator_5_eq));
  Comparator #(.mode("unsigned"), .width(5)) comparator_5 (
    .a(WriteIndex), .b(5'b10001), .eq(comparator_5_eq));  // open: gt, lt
  Comparator #(.mode("unsigned"), .width(5)) comparator_6 (
    .a(WriteIndex), .b(5'b10101), .eq(comparator_6_eq));  // open: gt, lt
  Comparator #(.mode("unsigned"), .width(5)) comparator_7 (
    .a(WriteIndex), .b(5'b11001), .eq(comparator_7_eq));  // open: gt, lt
  Comparator #(.mode("unsigned"), .width(5)) comparator_8 (
    .a(WriteIndex), .b(5'b11101), .eq(comparator_8_eq));  // open: gt, lt
  Register #(.width(32)) register_1 (.D(multiplexer_2_out), .en(RegWEn), .clk(clk), .Q(ra));  // open: clr
  Multiplexer #(.width(32)) multiplexer_2 (.in0(ra), .in1(WriteData), .out(multiplexer_2_out), .sel(comparator_1_eq));
  Multiplexer #(.width(32)) multiplexer_3 (.in0(t0), .in1(WriteData), .out(multiplexer_3_out), .sel(comparator_2_eq));
  Multiplexer #(.width(32)) multiplexer_4 (.in0(s1), .in1(WriteData), .out(multiplexer_4_out), .sel(comparator_3_eq));
  Multiplexer #(.width(32)) multiplexer_5 (.in0(a3), .in1(WriteData), .out(multiplexer_5_out), .sel(comparator_4_eq));
  Register #(.width(32)) register_2 (.D(multiplexer_1_out), .en(RegWEn), .clk(clk), .Q(a7));  // open: clr
  Register #(.width(32)) register_3 (.D(multiplexer_6_out), .en(RegWEn), .clk(clk), .Q(s5));  // open: clr
  Multiplexer #(.width(32)) multiplexer_6 (.in0(s5), .in1(WriteData), .out(multiplexer_6_out), .sel(comparator_6_eq));
  Register #(.width(32)) register_4 (.D(multiplexer_7_out), .en(RegWEn), .clk(clk), .Q(s9));  // open: clr
  Multiplexer #(.width(32)) multiplexer_7 (.in0(s9), .in1(WriteData), .out(multiplexer_7_out), .sel(comparator_7_eq));
  Register #(.width(32)) register_5 (.D(multiplexer_8_out), .en(RegWEn), .clk(clk), .Q(t4));  // open: clr
  Multiplexer #(.width(32)) multiplexer_8 (.in0(t4), .in1(WriteData), .out(multiplexer_8_out), .sel(comparator_8_eq));
  Register #(.width(32)) register_6 (.D(multiplexer_3_out), .en(RegWEn), .clk(clk), .Q(t0));  // open: clr
  Register #(.width(32)) register_7 (.D(multiplexer_4_out), .en(RegWEn), .clk(clk), .Q(s1));  // open: clr
  Register #(.width(32)) register_8 (.D(multiplexer_5_out), .en(RegWEn), .clk(clk), .Q(a3));  // open: clr
  Comparator #(.mode("unsigned"), .width(5)) comparator_9 (
    .a(WriteIndex), .b(5'b00010), .eq(comparator_9_eq));  // open: gt, lt
  Comparator #(.mode("unsigned"), .width(5)) comparator_10 (
    .a(WriteIndex), .b(5'b00110), .eq(comparator_10_eq));  // open: gt, lt
  Comparator #(.mode("unsigned"), .width(5)) comparator_11 (
    .a(WriteIndex), .b(5'b01010), .eq(comparator_11_eq));  // open: gt, lt
  Comparator #(.mode("unsigned"), .width(5)) comparator_12 (
    .a(WriteIndex), .b(5'b01110), .eq(comparator_12_eq));  // open: gt, lt
  Comparator #(.mode("unsigned"), .width(5)) comparator_13 (
    .a(WriteIndex), .b(5'b10010), .eq(comparator_13_eq));  // open: gt, lt
  Comparator #(.mode("unsigned"), .width(5)) comparator_14 (
    .a(WriteIndex), .b(5'b10110), .eq(comparator_14_eq));  // open: gt, lt
  Comparator #(.mode("unsigned"), .width(5)) comparator_15 (
    .a(WriteIndex), .b(5'b11010), .eq(comparator_15_eq));  // open: gt, lt
  Comparator #(.mode("unsigned"), .width(5)) comparator_16 (
    .a(WriteIndex), .b(5'b11110), .eq(comparator_16_eq));  // open: gt, lt
  Multiplexer #(.width(32)) multiplexer_9 (.in0(sp), .in1(WriteData), .out(multiplexer_9_out), .sel(comparator_9_eq));
  Multiplexer #(.width(32)) multiplexer_10 (
    .in0(t1), .in1(WriteData), .out(multiplexer_10_out), .sel(comparator_10_eq));
  Multiplexer #(.width(32)) multiplexer_11 (
    .in0(a0), .in1(WriteData), .out(multiplexer_11_out), .sel(comparator_11_eq));
  Multiplexer #(.width(32)) multiplexer_12 (
    .in0(a4), .in1(WriteData), .out(multiplexer_12_out), .sel(comparator_12_eq));
  Multiplexer #(.width(32)) multiplexer_13 (
    .in0(s2), .in1(WriteData), .out(multiplexer_13_out), .sel(comparator_13_eq));
  Multiplexer #(.width(32)) multiplexer_14 (
    .in0(s6), .in1(WriteData), .out(multiplexer_14_out), .sel(comparator_14_eq));
  Multiplexer #(.width(32)) multiplexer_15 (
    .in0(s10), .in1(WriteData), .out(multiplexer_15_out), .sel(comparator_15_eq));
  Multiplexer #(.width(32)) multiplexer_16 (
    .in0(t5), .in1(WriteData), .out(multiplexer_16_out), .sel(comparator_16_eq));
  Multiplexer #(.select(5), .width(32)) multiplexer_17 (
    .in0({32{1'b0}}), .in1(ra), .in2(sp), .in3(gp), .in4(tp), .in5(t0), .in6(t1), .in7(t2), .in8(s0),
    .in9(s1), .in10(a0), .in11(a1), .in12(a2), .in13(a3), .in14(a4), .in15(a5), .in16(a6), .in17(a7),
    .in18(s2), .in19(s3), .in20(s4), .in21(s5), .in22(s6), .in23(s7), .in24(s8), .in25(s9), .in26(s10),
    .in27(s11), .in28(t3), .in29(t4), .in30(t5), .in31(t6), .out(ReadData1), .sel(ReadIndex1));
  Register #(.width(32)) register_9 (.D(multiplexer_9_out), .en(RegWEn), .clk(clk), .Q(sp));  // open: clr
  Register #(.width(32)) register_10 (.D(multiplexer_10_out), .en(RegWEn), .clk(clk), .Q(t1));  // open: clr
  Register #(.width(32)) register_11 (.D(multiplexer_11_out), .en(RegWEn), .clk(clk), .Q(a0));  // open: clr
  Register #(.width(32)) register_12 (.D(multiplexer_12_out), .en(RegWEn), .clk(clk), .Q(a4));  // open: clr
  Register #(.width(32)) register_13 (.D(multiplexer_13_out), .en(RegWEn), .clk(clk), .Q(s2));  // open: clr
  Register #(.width(32)) register_14 (.D(multiplexer_14_out), .en(RegWEn), .clk(clk), .Q(s6));  // open: clr
  Register #(.width(32)) register_15 (.D(multiplexer_15_out), .en(RegWEn), .clk(clk), .Q(s10));  // open: clr
  Register #(.width(32)) register_16 (.D(multiplexer_16_out), .en(RegWEn), .clk(clk), .Q(t5));  // open: clr
  Comparator #(.mode("unsigned"), .width(5)) comparator_17 (
    .a(WriteIndex), .b(5'b00011), .eq(comparator_17_eq));  // open: gt, lt
  Comparator #(.mode("unsigned"), .width(5)) comparator_18 (
    .a(WriteIndex), .b(5'b00111), .eq(comparator_18_eq));  // open: gt, lt
  Comparator #(.mode("unsigned"), .width(5)) comparator_19 (
    .a(WriteIndex), .b(5'b01011), .eq(comparator_19_eq));  // open: gt, lt
  Comparator #(.mode("unsigned"), .width(5)) comparator_20 (
    .a(WriteIndex), .b(5'b01111), .eq(comparator_20_eq));  // open: gt, lt
  Comparator #(.mode("unsigned"), .width(5)) comparator_21 (
    .a(WriteIndex), .b(5'b10011), .eq(comparator_21_eq));  // open: gt, lt
  Comparator #(.mode("unsigned"), .width(5)) comparator_22 (
    .a(WriteIndex), .b(5'b10111), .eq(comparator_22_eq));  // open: gt, lt
  Comparator #(.mode("unsigned"), .width(5)) comparator_23 (
    .a(WriteIndex), .b(5'b11011), .eq(comparator_23_eq));  // open: gt, lt
  Comparator #(.mode("unsigned"), .width(5)) comparator_24 (
    .a(WriteIndex), .b({5{1'b1}}), .eq(comparator_24_eq));  // open: gt, lt
  Multiplexer #(.width(32)) multiplexer_18 (
    .in0(gp), .in1(WriteData), .out(multiplexer_18_out), .sel(comparator_17_eq));
  Multiplexer #(.width(32)) multiplexer_19 (
    .in0(t2), .in1(WriteData), .out(multiplexer_19_out), .sel(comparator_18_eq));
  Multiplexer #(.width(32)) multiplexer_20 (
    .in0(a1), .in1(WriteData), .out(multiplexer_20_out), .sel(comparator_19_eq));
  Multiplexer #(.width(32)) multiplexer_21 (
    .in0(a5), .in1(WriteData), .out(multiplexer_21_out), .sel(comparator_20_eq));
  Multiplexer #(.width(32)) multiplexer_22 (
    .in0(s3), .in1(WriteData), .out(multiplexer_22_out), .sel(comparator_21_eq));
  Multiplexer #(.width(32)) multiplexer_23 (
    .in0(s7), .in1(WriteData), .out(multiplexer_23_out), .sel(comparator_22_eq));
  Multiplexer #(.width(32)) multiplexer_24 (
    .in0(s11), .in1(WriteData), .out(multiplexer_24_out), .sel(comparator_23_eq));
  Multiplexer #(.width(32)) multiplexer_25 (
    .in0(t6), .in1(WriteData), .out(multiplexer_25_out), .sel(comparator_24_eq));
  Register #(.width(32)) register_17 (.D(multiplexer_18_out), .en(RegWEn), .clk(clk), .Q(gp));  // open: clr
  Register #(.width(32)) register_18 (.D(multiplexer_19_out), .en(RegWEn), .clk(clk), .Q(t2));  // open: clr
  Register #(.width(32)) register_19 (.D(multiplexer_20_out), .en(RegWEn), .clk(clk), .Q(a1));  // open: clr
  Register #(.width(32)) register_20 (.D(multiplexer_21_out), .en(RegWEn), .clk(clk), .Q(a5));  // open: clr
  Register #(.width(32)) register_21 (.D(multiplexer_22_out), .en(RegWEn), .clk(clk), .Q(s3));  // open: clr
  Register #(.width(32)) register_22 (.D(multiplexer_23_out), .en(RegWEn), .clk(clk), .Q(s7));  // open: clr
  Register #(.width(32)) register_23 (.D(multiplexer_24_out), .en(RegWEn), .clk(clk), .Q(s11));  // open: clr
  Register #(.width(32)) register_24 (.D(multiplexer_25_out), .en(RegWEn), .clk(clk), .Q(t6));  // open: clr
  Multiplexer #(.select(5), .width(32)) multiplexer_26 (
    .in0({32{1'b0}}), .in1(ra), .in2(sp), .in3(gp), .in4(tp), .in5(t0), .in6(t1), .in7(t2), .in8(s0),
    .in9(s1), .in10(a0), .in11(a1), .in12(a2), .in13(a3), .in14(a4), .in15(a5), .in16(a6), .in17(a7),
    .in18(s2), .in19(s3), .in20(s4), .in21(s5), .in22(s6), .in23(s7), .in24(s8), .in25(s9), .in26(s10),
    .in27(s11), .in28(t3), .in29(t4), .in30(t5), .in31(t6), .out(ReadData2), .sel(ReadIndex2));
  Comparator #(.mode("unsigned"), .width(5)) comparator_25 (
    .a(WriteIndex), .b(5'b00100), .eq(comparator_25_eq));  // open: gt, lt
  Comparator #(.mode("unsigned"), .width(5)) comparator_26 (
    .a(WriteIndex), .b(5'b10000), .eq(comparator_26_eq));  // open: gt, lt
  Comparator #(.mode("unsigned"), .width(5)) comparator_27 (
    .a(WriteIndex), .b(5'b10100), .eq(comparator_27_eq));  // open: gt, lt
  Multiplexer #(.width(32)) multiplexer_27 (
    .in0(tp), .in1(WriteData), .out(multiplexer_27_out), .sel(comparator_25_eq));
  Multiplexer #(.width(32)) multiplexer_28 (
    .in0(s0), .in1(WriteData), .out(multiplexer_28_out), .sel(comparator_28_eq));
  Comparator #(.mode("unsigned"), .width(5)) comparator_28 (
    .a(WriteIndex), .b(5'b01000), .eq(comparator_28_eq));  // open: gt, lt
  Multiplexer #(.width(32)) multiplexer_29 (
    .in0(a2), .in1(WriteData), .out(multiplexer_29_out), .sel(comparator_29_eq));
  Comparator #(.mode("unsigned"), .width(5)) comparator_29 (
    .a(WriteIndex), .b(5'b01100), .eq(comparator_29_eq));  // open: gt, lt
  Multiplexer #(.width(32)) multiplexer_30 (
    .in0(a6), .in1(WriteData), .out(multiplexer_30_out), .sel(comparator_26_eq));
  Multiplexer #(.width(32)) multiplexer_31 (
    .in0(s4), .in1(WriteData), .out(multiplexer_31_out), .sel(comparator_27_eq));
  Multiplexer #(.width(32)) multiplexer_32 (
    .in0(s8), .in1(WriteData), .out(multiplexer_32_out), .sel(comparator_30_eq));
  Comparator #(.mode("unsigned"), .width(5)) comparator_30 (
    .a(WriteIndex), .b(5'b11000), .eq(comparator_30_eq));  // open: gt, lt
  Multiplexer #(.width(32)) multiplexer_33 (
    .in0(t3), .in1(WriteData), .out(multiplexer_33_out), .sel(comparator_31_eq));
  Comparator #(.mode("unsigned"), .width(5)) comparator_31 (
    .a(WriteIndex), .b(5'b11100), .eq(comparator_31_eq));  // open: gt, lt
  Register #(.width(32)) register_25 (.D(multiplexer_27_out), .en(RegWEn), .clk(clk), .Q(tp));  // open: clr
  Register #(.width(32)) register_26 (.D(multiplexer_28_out), .en(RegWEn), .clk(clk), .Q(s0));  // open: clr
  Register #(.width(32)) register_27 (.D(multiplexer_29_out), .en(RegWEn), .clk(clk), .Q(a2));  // open: clr
  Register #(.width(32)) register_28 (.D(multiplexer_30_out), .en(RegWEn), .clk(clk), .Q(a6));  // open: clr
  Register #(.width(32)) register_29 (.D(multiplexer_31_out), .en(RegWEn), .clk(clk), .Q(s4));  // open: clr
  Register #(.width(32)) register_30 (.D(multiplexer_32_out), .en(RegWEn), .clk(clk), .Q(s8));  // open: clr
  Register #(.width(32)) register_31 (.D(multiplexer_33_out), .en(RegWEn), .clk(clk), .Q(t3));  // open: clr

  // Notes on the sheet:
  //   INPUTS to your circuit
  //   DON'T CHANGE THE LOCATIONS OF THE INPUTS AND OUTPUTS!
  //   These are DEBUG/TEST outputs from your circuit.
  //   OUTPUTS from your circuit
endmodule
